// Logisim project projeto.circ as structural Verilog: 5 circuits, main circuit main
module main (
  input  Jogador,
  input  Jogar,
  input  Jogador_0,
  input  in_4,
  input  in_5,
  input  in_6,
  input  in_7,
  input  Jogador_1,
  input  in_9,
  input  in_10
);

  wire comparador_1_maior, comparador_1_menor, comparador_1_out_8, decode_1_out_5, decode_1_out_6,
       decode_1_out_7, decode_1_out_8, decode_1_out_9, decode_1_out_10, decode_1_out_11, decode_2_out_5,
       decode_2_out_6, decode_2_out_7, decode_2_out_8, decode_2_out_9, decode_2_out_10, decode_2_out_11,
       mux_4_4_1_out_10, mux_4_4_1_out_11, mux_4_4_1_out_12, mux_4_4_1_out_13;

  decode decode_1 (
    .out_5(decode_1_out_5), .out_6(decode_1_out_6), .out_7(decode_1_out_7), .out_8(decode_1_out_8),
    .out_9(decode_1_out_9), .out_10(decode_1_out_10), .out_11(decode_1_out_11), .in_1(Jogador_0),
    .in_2(in_4), .in_3(in_5), .in_4(in_6));
  _7_Segment_Display u_7_segment_display_1 (
    .g(decode_1_out_11), .f(decode_1_out_10), .a(decode_1_out_5), .b(decode_1_out_6), .e(decode_1_out_9),
    .d(decode_1_out_8), .c(decode_1_out_7));  // open: dp
  decode decode_2 (
    .out_5(decode_2_out_5), .out_6(decode_2_out_6), .out_7(decode_2_out_7), .out_8(decode_2_out_8),
    .out_9(decode_2_out_9), .out_10(decode_2_out_10), .out_11(decode_2_out_11), .in_1(in_7),
    .in_2(Jogador_1), .in_3(in_9), .in_4(in_10));
  _7_Segment_Display u_7_segment_display_2 (
    .g(decode_2_out_11), .f(decode_2_out_10), .a(decode_2_out_5), .b(decode_2_out_6), .e(decode_2_out_9),
    .d(decode_2_out_8), .c(decode_2_out_7));  // open: dp
  Comparador comparador_1 (
    .in_2(mux_4_4_1_out_10), .in_3(mux_4_4_1_out_11), .in_4(mux_4_4_1_out_12), .in_5(mux_4_4_1_out_13),
    .in_1(Jogar), .maior(comparador_1_maior), .menor(comparador_1_menor), .out_8(comparador_1_out_8));
  Mux_4_4 mux_4_4_1 (
    ._1_0(Jogador_0), ._1_1(in_7), ._2_0(in_4), ._2_1(Jogador_1), ._3_0(in_5), ._3_1(in_9), ._4_0(in_6),
    ._4_1(in_10), .S(Jogador), .out_10(mux_4_4_1_out_10), .out_11(mux_4_4_1_out_11),
    .out_12(mux_4_4_1_out_12), .out_13(mux_4_4_1_out_13));
  LED led_1 (.in(comparador_1_maior));
  LED led_2 (.in(comparador_1_menor));
  LED led_3 (.in(comparador_1_out_8));

  // Notes on the sheet:
  //   Acertou
  //   maior
  //   menor
  //   Como jogar ?
  //   1-> Escolha um jogador (0 ou 1)
  //   3-> Escolha um número entre 0 e 15 em formato binário
  //   4-> Altere jogar para 1, assim fará sua jogada
  //   2-> Cada jogador chuta um número na sua determinada área indicada
  //   5-> De acordo com a dica faça sua próxima tentativa depois do outro jogador,se não perdeu 
endmodule

module multiplexador (
  input  in_1,
  input  in_2,
  input  in_3,
  output out_4
);

  wire and_1_out, and_2_out, and_3_out, and_4_out;

  and and_1 (and_1_out, ~in_1, in_2, in_3);  // AND_Gate
  and and_2 (and_2_out, in_1, ~in_2, ~in_3);  // AND_Gate
  and and_3 (and_3_out, in_1, in_2, ~in_3);  // AND_Gate
  and and_4 (and_4_out, in_1, in_2, in_3);
  or or_1 (out_4, and_1_out, and_2_out, and_3_out, and_4_out);

  // Notes on the sheet:
  //   Multiplexador 1
endmodule

module Mux_4_4 (
  input  S,
  input  _1_0,
  input  _1_1,
  input  _2_0,
  input  _2_1,
  input  _3_0,
  input  _3_1,
  input  _4_0,
  input  _4_1,
  output out_10,
  output out_11,
  output out_12,
  output out_13
);

  multiplexador multiplexador_1 (.in_1(_1_0), .in_2(_1_1), .in_3(S), .out_4(out_10));
  multiplexador multiplexador_2 (.in_1(_2_0), .in_2(_2_1), .in_3(S), .out_4(out_11));
  multiplexador multiplexador_3 (.in_1(_3_0), .in_2(_3_1), .in_3(S), .out_4(out_12));
  multiplexador multiplexador_4 (.in_1(_4_0), .in_2(_4_1), .in_3(S), .out_4(out_13));
endmodule

module decode (
  input  in_1,
  input  in_2,
  input  in_3,
  input  in_4,
  output out_5,
  output out_6,
  output out_7,
  output out_8,
  output out_9,
  output out_10,
  output out_11
);

  wire and_1_out, and_2_out, and_3_out, and_4_out, and_5_out, and_6_out, and_7_out, and_8_out, and_9_out,
       and_10_out, and_11_out, and_12_out, and_13_out, and_14_out, and_15_out, and_16_out, and_17_out,
       and_18_out, and_19_out, and_20_out, and_21_out, and_22_out, and_23_out, and_24_out, and_25_out,
       and_26_out, and_27_out, and_28_out, and_29_out, and_30_out, and_31_out, and_32_out, and_33_out,
       and_34_out, and_35_out, and_36_out, and_37_out, and_38_out, and_39_out, and_40_out, and_41_out,
       and_42_out, and_43_out, and_44_out, and_45_out, and_46_out, and_47_out, and_48_out, and_49_out,
       and_50_out, and_51_out, and_52_out, and_53_out, and_54_out, and_55_out, and_56_out, and_57_out,
       and_58_out, and_59_out, and_60_out, and_61_out, and_62_out, and_63_out, and_64_out, and_65_out,
       and_66_out, and_67_out, and_68_out, and_69_out, and_70_out, and_71_out, and_72_out, and_73_out,
       and_74_out, and_75_out, and_76_out, and_77_out, and_78_out, and_79_out;

  and and_1 (and_1_out, ~in_1, ~in_2, ~in_3, ~in_4);  // AND_Gate
  and and_2 (and_2_out, ~in_1, ~in_2, in_3, ~in_4);  // AND_Gate
  and and_3 (and_3_out, ~in_1, ~in_2, in_3, in_4);  // AND_Gate
  and and_4 (and_4_out, ~in_1, in_2, ~in_3, in_4);  // AND_Gate
  and and_5 (and_5_out, ~in_1, in_2, in_3, ~in_4);  // AND_Gate
  and and_6 (and_6_out, ~in_1, in_2, in_3, in_4);  // AND_Gate
  and and_7 (and_7_out, in_1, ~in_2, ~in_3, ~in_4);  // AND_Gate
  and and_8 (and_8_out, in_1, ~in_2, ~in_3, in_4);  // AND_Gate
  and and_9 (and_9_out, in_1, ~in_2, in_3, ~in_4);  // AND_Gate
  and and_10 (and_10_out, in_1, in_2, ~in_3, ~in_4);  // AND_Gate
  and and_11 (and_11_out, in_1, in_2, in_3, ~in_4);  // AND_Gate
  and and_12 (and_12_out, in_1, in_2, in_3, ~in_4);  // AND_Gate
  and and_13 (and_13_out, in_1, in_2, in_3, in_4);
  and and_14 (and_14_out, ~in_1, ~in_2, ~in_3, ~in_4);  // AND_Gate
  and and_15 (and_15_out, ~in_1, ~in_2, ~in_3, in_4);  // AND_Gate
  and and_16 (and_16_out, ~in_1, ~in_2, in_3, ~in_4);  // AND_Gate
  and and_17 (and_17_out, ~in_1, ~in_2, in_3, in_4);  // AND_Gate
  and and_18 (and_18_out, ~in_1, ~in_2, in_3, in_4);  // AND_Gate
  and and_19 (and_19_out, ~in_1, in_2, in_3, in_4);  // AND_Gate
  and and_20 (and_20_out, ~in_1, in_2, ~in_3, ~in_4);  // AND_Gate
  and and_21 (and_21_out, in_1, ~in_2, ~in_3, ~in_4);  // AND_Gate
  and and_22 (and_22_out, in_1, ~in_2, ~in_3, in_4);  // AND_Gate
  and and_23 (and_23_out, in_1, ~in_2, in_3, ~in_4);  // AND_Gate
  and and_24 (and_24_out, in_1, in_2, ~in_3, in_4);  // AND_Gate
  and and_25 (and_25_out, ~in_1, ~in_2, ~in_3, ~in_4);  // AND_Gate
  and and_26 (and_26_out, ~in_1, ~in_2, ~in_3, in_4);  // AND_Gate
  and and_27 (and_27_out, ~in_1, ~in_2, in_3, in_4);  // AND_Gate
  and and_28 (and_28_out, ~in_1, in_2, ~in_3, ~in_4);  // AND_Gate
  and and_29 (and_29_out, ~in_1, in_2, ~in_3, in_4);  // AND_Gate
  and and_30 (and_30_out, ~in_1, in_2, in_3, ~in_4);  // AND_Gate
  and and_31 (and_31_out, ~in_1, in_2, in_3, in_4);  // AND_Gate
  and and_32 (and_32_out, in_1, ~in_2, ~in_3, ~in_4);  // AND_Gate
  and and_33 (and_33_out, in_1, ~in_2, ~in_3, in_4);  // AND_Gate
  and and_34 (and_34_out, in_1, ~in_2, in_3, ~in_4);  // AND_Gate
  and and_35 (and_35_out, in_1, in_2, ~in_3, in_4);  // AND_Gate
  and and_36 (and_36_out, in_1, ~in_2, in_3, in_4);  // AND_Gate
  and and_37 (and_37_out, ~in_1, ~in_2, ~in_3, ~in_4);  // AND_Gate
  and and_38 (and_38_out, ~in_1, ~in_2, in_3, ~in_4);  // AND_Gate
  and and_39 (and_39_out, ~in_1, ~in_2, in_3, in_4);  // AND_Gate
  and and_40 (and_40_out, ~in_1, in_2, ~in_3, in_4);  // AND_Gate
  and and_41 (and_41_out, ~in_1, in_2, in_3, ~in_4);  // AND_Gate
  and and_42 (and_42_out, in_1, ~in_2, ~in_3, ~in_4);  // AND_Gate
  and and_43 (and_43_out, in_1, ~in_2, in_3, in_4);  // AND_Gate
  and and_44 (and_44_out, in_1, in_2, ~in_3, ~in_4);  // AND_Gate
  and and_45 (and_45_out, in_1, in_2, ~in_3, in_4);  // AND_Gate
  and and_46 (and_46_out, in_1, in_2, in_3, ~in_4);  // AND_Gate
  and and_47 (and_47_out, ~in_1, ~in_2, ~in_3, ~in_4);  // AND_Gate
  and and_48 (and_48_out, ~in_1, ~in_2, in_3, ~in_4);  // AND_Gate
  and and_49 (and_49_out, ~in_1, in_2, in_3, ~in_4);  // AND_Gate
  and and_50 (and_50_out, in_1, ~in_2, ~in_3, ~in_4);  // AND_Gate
  and and_51 (and_51_out, in_1, ~in_2, in_3, ~in_4);  // AND_Gate
  and and_52 (and_52_out, in_1, ~in_2, in_3, in_4);  // AND_Gate
  and and_53 (and_53_out, in_1, in_2, ~in_3, ~in_4);  // AND_Gate
  and and_54 (and_54_out, in_1, in_2, ~in_3, in_4);  // AND_Gate
  and and_55 (and_55_out, in_1, in_2, in_3, ~in_4);  // AND_Gate
  and and_56 (and_56_out, in_1, in_2, in_3, in_4);
  and and_57 (and_57_out, ~in_1, ~in_2, ~in_3, ~in_4);  // AND_Gate
  and and_58 (and_58_out, ~in_1, in_2, ~in_3, ~in_4);  // AND_Gate
  and and_59 (and_59_out, ~in_1, in_2, ~in_3, in_4);  // AND_Gate
  and and_60 (and_60_out, ~in_1, in_2, in_3, ~in_4);  // AND_Gate
  and and_61 (and_61_out, in_1, ~in_2, ~in_2, ~in_4);  // AND_Gate
  and and_62 (and_62_out, in_1, ~in_2, ~in_3, in_4);  // AND_Gate
  and and_63 (and_63_out, in_1, ~in_2, in_3, ~in_4);  // AND_Gate
  and and_64 (and_64_out, in_1, ~in_2, in_3, in_4);  // AND_Gate
  and and_65 (and_65_out, in_1, in_2, ~in_3, ~in_4);  // AND_Gate
  and and_66 (and_66_out, in_1, in_2, in_3, ~in_4);  // AND_Gate
  and and_67 (and_67_out, in_1, in_2, in_3, in_4);
  and and_68 (and_68_out, ~in_1, ~in_2, in_3, ~in_4);  // AND_Gate
  and and_69 (and_69_out, ~in_1, ~in_2, in_3, in_4);  // AND_Gate
  and and_70 (and_70_out, ~in_1, in_2, ~in_3, ~in_4);  // AND_Gate
  and and_71 (and_71_out, ~in_1, in_2, ~in_3, in_4);  // AND_Gate
  and and_72 (and_72_out, ~in_1, in_2, in_3, ~in_4);  // AND_Gate
  and and_73 (and_73_out, in_1, ~in_2, ~in_3, ~in_4);  // AND_Gate
  and and_74 (and_74_out, in_1, ~in_2, ~in_3, in_4);  // AND_Gate
  and and_75 (and_75_out, in_1, ~in_2, in_3, ~in_4);  // AND_Gate
  and and_76 (and_76_out, in_1, ~in_2, in_3, in_4);  // AND_Gate
  and and_77 (and_77_out, in_1, in_2, ~in_3, in_4);  // AND_Gate
  and and_78 (and_78_out, in_1, in_2, in_3, ~in_4);  // AND_Gate
  and and_79 (and_79_out, in_1, in_2, in_3, in_4);
  or A (out_5, and_1_out, and_2_out, and_3_out, and_4_out, and_5_out, and_6_out, and_13_out, and_7_out, and_8_out, and_9_out, and_10_out, and_11_out, and_12_out);
  or B (out_6, and_14_out, and_15_out, and_16_out, and_17_out, and_18_out, and_19_out, and_20_out, and_21_out, and_22_out, and_23_out, and_24_out);
  or C (out_7, and_25_out, and_26_out, and_27_out, and_28_out, and_29_out, and_30_out, and_31_out, and_32_out, and_33_out, and_34_out, and_35_out, and_36_out);
  or D (out_8, and_37_out, and_38_out, and_39_out, and_40_out, and_41_out, and_42_out, and_43_out, and_44_out, and_45_out, and_46_out);
  or E (out_9, and_47_out, and_48_out, and_49_out, and_50_out, and_51_out, and_52_out, and_53_out, and_54_out, and_55_out, and_56_out);
  or F (out_10, and_57_out, and_58_out, and_59_out, and_60_out, and_61_out, and_62_out, and_63_out, and_64_out, and_65_out, and_66_out, and_67_out);
  or G (out_11, and_68_out, and_69_out, and_70_out, and_71_out, and_72_out, and_73_out, and_74_out, and_75_out, and_76_out, and_77_out, and_78_out, and_79_out);

  // Notes on the sheet:
  //   --------------------------------------------------------------------------------------
endmodule

// Game
module Comparador (
  input  in_1,
  input  in_2,
  input  in_3,
  input  in_4,
  input  in_5,
  output maior,
  output menor,
  output out_8
);

  wire and_1_out, and_2_out, and_3_out, and_5_out, nor_1_out, or_1_out, xnor_1_out, xnor_2_out, xnor_3_out,
       xnor_4_out;

  xnor xnor_1 (xnor_1_out, in_2, 1'b1);
  xnor xnor_2 (xnor_2_out, in_3, 1'b0);
  xnor xnor_3 (xnor_3_out, in_4, 1'b1);
  xnor xnor_4 (xnor_4_out, in_5, 1'b0);
  and and_1 (and_1_out, in_2, ~1'b1);  // AND_Gate
  and and_2 (and_2_out, xnor_1_out, in_3, ~1'b0);  // AND_Gate
  and and_3 (and_3_out, xnor_1_out, xnor_2_out, in_2, ~1'b1);  // AND_Gate
  and and_4 (and_3_out, xnor_1_out, xnor_2_out, xnor_3_out, in_2, ~1'b1);  // AND_Gate
  and and_5 (and_5_out, xnor_1_out, xnor_2_out, xnor_3_out, xnor_4_out);
  or or_1 (or_1_out, and_1_out, and_2_out, and_3_out, and_3_out);
  nor nor_1 (nor_1_out, and_5_out, or_1_out);
  and and_6 (maior, and_5_out, in_1);
  and and_7 (menor, nor_1_out, in_1);
  and and_8 (out_8, or_1_out, in_1);

  // Notes on the sheet:
  //   Escolha o número mágico!
  //   igual
endmodule
